# Fritzing sketch Diagrama_Eletrônica_Editável (saved by Fritzing 0.9.3b)
circuit board: 8.46667cm x 5.64444cm
breadboards: 1

parts:
  S1 = Pushbutton [package="[THT]"]
  S2 = Pushbutton [package="[THT]"]
  R2 = Resistor [tolerance=±5% resistance=10k package=THT]
  R1 = Resistor [tolerance=±5% resistance=10k package=THT]
  LED1 = LED - 5mm [color="Blue (525nm)" package="5 mm [THT]"]
  LED2 = LED - 5mm [color="Blue (525nm)" package="5 mm [THT]"]
  R3 = Resistor [tolerance=±5% resistance=220 package=THT]
  R4 = Resistor [tolerance=±5% resistance=220 package=THT]
  Componente1 = Arduino Nano (Rev3.0)
  Componente2 = Bluetooth HC-05 Macho
  R5 = Resistor [tolerance=±5% resistance=2.2k package=THT]
  R6 = Resistor [tolerance=±5% resistance=1k package=THT]
  K1 = OMRON PCB Power Relay – G5LE [part_number="G5LE-1\n" package=THT]
  K2 = OMRON PCB Power Relay – G5LE [part_number="G5LE-1\n" package=THT]
  K3 = OMRON PCB Power Relay – G5LE [part_number="G5LE-1\n" package=THT]
  K4 = OMRON PCB Power Relay – G5LE [part_number="G5LE-1\n" package=THT]

nets:
  N1: S1.Pin_1, S1.Pin_2, R2.Pin_1, R1.Pin_1, R3.Pin_0, Componente1.GND, R6.Pin_0, K1.COIL1, K2.COIL1, K3.COIL1, K4.COIL1
  N2: S1.Pin_3, S1.Pin_4, R1.Pin_0, Componente1.D4
  N3: S2.Pin_1, S2.Pin_2, Componente1.5V
  N4: S2.Pin_3, S2.Pin_4, R2.Pin_0, Componente1.D5
  N5: LED1.cathode, R3.Pin_1
  N6: LED1.anode, Componente1.D2
  N7: LED2.cathode, R4.Pin_1
  N8: LED2.anode, Componente1.D3
  N9: Componente1.D1/TX, R5.Pin_0
  N10: Componente1.D11/MOSI, K4.COIL2
  N11: Componente1.D12/MISO, K3.COIL2
  N12: Componente1.A1, K2.COIL2
  N13: Componente1.A0, K1.COIL2
  N14: Componente2.RXD, R5.Pin_1, R6.Pin_1

// code stored in the sketch: Automa__o_OFICINA_MAKER.ino
#define pinRele 11
#define pinrele2 10
#define  button A0
#include <SoftwareSerial.h>
 
SoftwareSerial btSerial(0, 1); // RX, TX
 
void setup() {
        
  pinMode(button, INPUT);    
  //Serial.begin(9600);
  
  pinMode(pinRele, OUTPUT);
  pinMode(pinrele2, OUTPUT);
  digitalWrite(pinRele, HIGH);
  digitalWrite(pinrele2, HIGH);
  btSerial.begin(9600);
  //Serial.begin(9600);

 
}
 
boolean estadobotao;
boolean estadobotao2;
boolean statusRele1 =HIGH; 
boolean statusRele2 = HIGH; 
String btComando;
String btComando2;




void loop() {


  
estadobotao = digitalRead(button);   
Serial.println (estadobotao);

estadobotao2 = digitalRead(button);   
Serial.println (estadobotao2);



//////////////////////////////////////////////////////////////////////////////////////////////////////////////////////////////////////////////////////////////////////////////////////////////////
 if (estadobotao == 0){    
     digitalWrite(pinRele, statusRele1); 
     statusRele1=!statusRele1;
     digitalWrite(pinrele2, statusRele2); 
     statusRele2=!statusRele2;
         Serial.println ("BluetoothConectadoForaoDoWhile");
    Serial.println ("-------------------------------");
    Serial.println (estadobotao);
    Serial.println ("*******************************");             
}               
  
    while (btSerial.available()) {
    Serial.println ("BluetoothConectadoDentroDoWhile");
    Serial.println ("-------------------------------");
    Serial.println (estadobotao);
    if (estadobotao == 0){
      digitalWrite(pinRele, statusRele1);
      statusRele1=!statusRele1;
       if (estadobotao2 == 0){ 
        digitalWrite(pinrele2, statusRele2); 
        statusRele2=!statusRele2;
       }
        
    }
    else{
      
     char comandoRec = btSerial.read();
     btComando += char( comandoRec );
     Serial.print(comandoRec);

     char comandoRec2 = btSerial.read();
     btComando2 += char( comandoRec2 );
     Serial.print(comandoRec2);
 
  
 
     if (comandoRec == ';') {
        if (btComando == "B1;") {
            statusRele1=!statusRele1;
            digitalWrite(pinRele, statusRele1);
        }
        btComando = "";
     }
    if (comandoRec2 == ';') {
        if (btComando2 == "B2;") {
            statusRele2=!statusRele2;
            digitalWrite(pinrele2, statusRele2);
        }
        btComando2 = "";            
        }   
   } 
   /*if (estadobotao2 == 0){
     digitalWrite(pinrele2, statusRele2); 
     statusRele2=!statusRele2;
    }
   
    else{
      
     char comandoRec2 = btSerial.read();
     btComando2 += char( comandoRec2 );
     Serial.print(comandoRec2);
 
     if (comandoRec2 == ';') {
        if (btComando2 == "B2;") {
            statusRele2=!statusRele2;
            digitalWrite(pinrele2, statusRele2);
        }
      btComando2 = "";            
}   
      
}           

     */
    }
////////////////////////////////////////////////////////////////////////////////////////////////////////////////////////////////////////////////////////////////////////////////////////////////////
 
 
if (estadobotao2 == 0) {       
Serial.println("PressionadoButton");
digitalWrite(pinrele2, statusRele2); 
statusRele2=!statusRele2;
delay(500);   
}
}

// code stored in the sketch: diagrama da placa.ino
#define pinRele 5
#define  button 4
#include <SoftwareSerial.h>
 
SoftwareSerial btSerial(0, 1); // RX, TX
 
void setup() {
        
  pinMode(button, INPUT);    
  Serial.begin(9600);
  
  pinMode(pinRele, OUTPUT);
  digitalWrite(pinRele, HIGH);
  btSerial.begin(9600);
  Serial.begin(9600);
}
 
boolean estadobotao;
boolean statusRele = HIGH; 
String btComando;


void loop() {


  
estadobotao = digitalRead(button);   
Serial.println (estadobotao);


 if (estadobotao == 0) {    
     digitalWrite(pinRele, statusRele); 
     statusRele=!statusRele;
         Serial.println ("BluetoothConectadoForaoDoWhile");
    Serial.println ("-------------------------------");
    Serial.println (estadobotao);
    Serial.println ("*******************************");             
}               
  
    while (btSerial.available()) {
    Serial.println ("BluetoothConectadoDentroDoWhile");
    Serial.println ("-------------------------------");
    Serial.println (estadobotao);
    if (estadobotao == 0){
      digitalWrite(pinRele, statusRele); 
     statusRele=!statusRele;
    }
    else{
      
     char comandoRec = btSerial.read();
     btComando += char( comandoRec );
     Serial.print(comandoRec);
 
     if (comandoRec == ';') {
        if (btComando == "B1;") {
            statusRele=!statusRele;
            digitalWrite(pinRele, statusRele);
        }
        btComando = "";
     }
    }                 
    }               
}
